# Fritzing sketch Secret Knock Box (saved by Fritzing 0.9.3b)
breadboards: 1

parts:
  J1 = Basic Servo
  Piezo_Disk = Piezo Speaker
  Pushbutton_Switch = Pushbutton [package="[SMD]"]
  R1 = Resistor [tolerance=±5% resistance=470k package=THT]
  Slide_Switch = SWITCH_SPDT [package=kps-1290]
  Vibration_Motor = Vibration Motor- ROB-08449 [package=vibe-motor-10mm]
  Part1 = Arduino Pro Mini (3.3V)
  4_5V = 3xAAA Switchable Battery Pack w/JST connector

nets:
  GND: J1.gnd, Piezo_Disk.pin1, Pushbutton_Switch.Pin_1, Pushbutton_Switch.Pin_2, R1.Pin_1, Vibration_Motor.-, Part1.GND, 4_5V.NEG
  N1: J1.vcc, Slide_Switch.P, Part1.RAW
  N2: J1.pulse, Part1.MOSI
  N3: Piezo_Disk.pin2, R1.Pin_0, Part1.A0
  N4: Pushbutton_Switch.Pin_3, Pushbutton_Switch.Pin_4, Part1.D10
  N5: Slide_Switch.O, 4_5V.POS
  N6: Vibration_Motor.+, Part1.MISO

custom parts:
  3xAAA Switchable Battery Pack w/JST connector: 3xAAA Switchable Battery Pack with JST connector
