# Fritzing sketch Secret Knock Treasure Book (saved by Fritzing 0.9.3b)
breadboards: 1

parts:
  part = Basic Servo
  Piezo_Disk = Piezo Speaker
  Pushbutton_Switch = Pushbutton [package="[SMD]"]
  R1 = Resistor [tolerance=±5% resistance=470k package=THT]
  Slide_Switch = SWITCH_SPDT [package=kps-1290]
  Vibration_Motor = Vibration Motor- ROB-08449 [package=vibe-motor-10mm]
  part_2 = Arduino Pro Mini (3.3V)
  4_5V = 3xAAA Switchable Battery Pack w/JST connector

nets:
  GND: part.gnd, Piezo_Disk.pin1, Pushbutton_Switch.Pin_1, Pushbutton_Switch.Pin_2, R1.Pin_1, Vibration_Motor.-, part_2.GND, 4_5V.NEG
  N1: part.vcc, Slide_Switch.P, part_2.RAW
  N2: part.pulse, part_2.MOSI
  N3: Piezo_Disk.pin2, R1.Pin_0, part_2.A0
  N4: Pushbutton_Switch.Pin_3, Pushbutton_Switch.Pin_4, part_2.D10
  N5: Slide_Switch.O, 4_5V.POS
  N6: Vibration_Motor.+, part_2.MISO

custom parts:
  3xAAA Switchable Battery Pack w/JST connector: 3xAAA Switchable Battery Pack with JST connector
